// Digital circuit 4bit_CPU.dig as structural Verilog
module _4bit_CPU (
);

  wire Counter_p1;
  wire [3:0] ir_1_instruction, ramblock_1_p3;

  // ProgramCounter Counter: pin names not known; wires that end beside it: Counter_p1
  // ramBlock ramblock_1: pin names not known; wires that end beside it: Counter_p1, Counter_p1, ramblock_1_p3
  IR ir_1 (.Data(ramblock_1_p3), .Instruction(ir_1_instruction));  // open: Clock
  // _4bit_ALU _4bit_alu_1: pin names not known; wires that end beside it: ir_1_instruction
  RegisterFile registerfile_1 ();  // open: Clock, Clear, Zero_Flag, Clear_2, Zero_Flag_2, Write_Register, Write_Data, Read_Reg1, Read_Reg2, R1, R2
endmodule
