// Digital circuit IR.dig as structural Verilog
module IR (
  input  [3:0] Data,
  input  Clock,
  output [3:0] Instruction
);

  // Register register_1: pin names not known; wires that end beside it: Clock, Data, Instruction
endmodule
