// Digital circuit ProgramCounter.dig as structural Verilog
module ProgramCounter (
  input  Clock,
  input  [3:0] Default_Val,
  input  [3:0] constant,
  input  cin,
  input  Selector,
  output [3:0] \output 
);

  wire [3:0] _4bit_full_adder_1_p4, multiplexer_1_out;

  Multiplexer #(.Bits(4)) multiplexer_1 (
    .sel(Selector), .in_0(Default_Val), .in_1(_4bit_full_adder_1_p4), .out(multiplexer_1_out));
  // Register register_1: pin names not known; wires that end beside it: Clock, multiplexer_1_out, \output 
  // _4bit_full_adder _4bit_full_adder_1: pin names not known; wires that end beside it: \output , constant, cin, _4bit_full_adder_1_p4

  // Notes on the sheet:
  //   constant: default 1
endmodule
